# Fritzing sketch schematic_V2 (saved by Fritzing 0.9.3b)
circuit board: 7cm x 5cm
breadboards: 1

parts:
  Part2 = RedBear-Duo
  DHT22 = DHT22 Humidity and Temperature Sensor
  PPD42NJ = Grove Dust Sensor
  MQ135 = Gas Sensor Breakout Board
  MQ7 = Gas Sensor Breakout Board
  R1 = Resistor [tolerance=±5% resistance=220 package="2010 [SMD]"]
  Part3 = Adafruit Ultimate GPS v3 [part_number="Adafruit #746"]

nets:
  N1: Part2.A4, MQ135.AOUT
  N2: Part2.A5, MQ7.AOUT
  N3: Part2.RX, Part3.TX
  N4: Part2.TX, Part3.RX
  GND: Part2.GND, DHT22.GND, PPD42NJ.GND, MQ135.GND, MQ7.GND, Part3.GND
  5V: Part2.VIN, PPD42NJ.VCC, MQ135.5V, MQ7.5V
  N5: Part2.D0, DHT22.DATA, R1.Pin_0
  N6: Part2.D1, MQ7.DOUT
  N7: Part2.D5, PPD42NJ.SIG
  3V3: Part2.3V3, DHT22.VDD, R1.Pin_1, Part3.3.3V

custom parts:
  RedBear-Duo: Duo is a thumb-size development board made to simplify the building process of Internet of Things (IoT). This part is a modification of the Particle Photon part by Brett Walach,Fabian Althaus
  Grove Dust Sensor: PPD42 Grove Dust Sensor
  Gas Sensor Breakout Board: Gas sensor breakout board. Input voltage is 5V. Sensor output is available in analog and digital.
  Adafruit Ultimate GPS v3: We carry a few different GPS modules here in the Adafruit shop, but none that satisfied our every desire - that's why we designed this little GPS breakout board. We believe this is the Ultimate GPS module, so we named it that. It's got everything you want and more: -165 dBm sensitivity, 10 Hz updates, 66 channels 5V friendly design and only 20mA current draw Breadboard friendly + two mounting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
